// Logisim project aiAlu.circ as structural Verilog
module Half_Adder (
  input  a,
  input  b,
  output out_3,
  output out_4
);

  xor xor_1 (out_3, b, a);
  and and_1 (out_4, b, a);
endmodule
